# Fritzing sketch pi-robot-board (saved by Fritzing 0.9.3b)
circuit board: 4.86cm x 4.80718cm
breadboards: 1

parts:
  J1 = double row female pin header, 26 pins [form="♀ (female)"]
  IC1 = H-Bridge [package=THT]
  Pad1 = Pad [width=10.16 height=3.2926019999999996 connect=center]  # not connected
  Battery = screw terminal, 2 pins
  Right_Motor_Out = screw terminal, 2 pins
  Left_Motor_Out = screw terminal, 2 pins

nets:
  GND1: J1.pin1, IC1.GND1, IC1.GND2, IC1.GND3, IC1.GND4, Battery.pin1
  N1: J1.pin14, IC1.VCC1
  N2: J1.pin17, IC1.4A
  N3: J1.pin18, IC1.3A
  N4: J1.pin25, IC1.2A
  N5: J1.pin26, IC1.1A
  N6: IC1.1Y, Left_Motor_Out.pin1
  N7: IC1.2Y, Left_Motor_Out.pin2
  N8: IC1.VCC2, Battery.pin2
  N9: IC1.3Y, Right_Motor_Out.pin2
  N10: IC1.4Y, Right_Motor_Out.pin1

notes:
  +
  -
  Left
  v0.4
  Right
  pi-robo-board
